# Fritzing sketch ESP32 (saved by Fritzing 1.0.6)
breadboards: 1

parts:
  Mod1 = Amica NodeMCU DEVKIT 1.0
  LED1 = LEDs [package=led10mm]  # not connected
  R1 = Resistor [tolerance=±5% resistance=220 package="2010 [SMD]"]

nets:
  N1: Mod1.pin1, Mod1.pin_10, Mod1.pin_26
  N2: Mod1.pin2, Mod1.pin_9, Mod1.pin_25, Mod1.pin_29
  N3: Mod1.pin_13, R1.Pin_1

notes:
  Wichtig !
  Anode über Wiederstand an Pin 2
  Kathode an GND
  192.168.4.1 ist die Webadresse
  SSID u. Passwort befindet sich im Code . Und kann geändert werden :)
